# Fritzing sketch 6502_computer (saved by Fritzing 0.9.3b)
breadboards: 6

parts:
  IC1 = 74HC08 Logic AND Gate [part_number=74HC08 package="DIP (Dual Inline) [THT]"]
  IC2 = IC, DIP package, 20 pins [chip_label=74HCT688E]
  IC3 = IC, DIP package, 20 pins [chip_label=74HCT688E]
  IC4 = IC, DIP package, 20 pins [chip_label=74HCT688E]
  IC5 = 74HC08 Logic AND Gate [part_number=74HC08 package="DIP (Dual Inline) [THT]"]
  Q1 = NPN-Transistor [package="TO92 [THT]"]
  IC6 = IC, DIP package, 16 pins [chip_label=74LS161A]
  Q2 = NPN-Transistor [package="TO92 [THT]"]
  U3 = 74HC595 [package="DIP16 [THT]"]
  U4 = 74HC595 [package="DIP16 [THT]"]
  IC7 = IC, DIP package, 20 pins [chip_label=74LS244AN]
  U5 = SWITCH_SPDT [package=kps-1290]
  IC8 = IC, DIP package, 40 pins [chip_label="WDC 65C02"]
  U6 = SWITCH_SPDT [package=kps-1290]
  IC9 = IC, DIP package, 14 pins [chip_label=74HC04]
  IC10 = IC, DIP package, 14 pins [chip_label=74HC04]
  IC11 = Voltage Regulator [package=to220-igo]
  XTAL1 = Crystal [frequency="1 MHz" package=THT]
  IC12 = 74HC08 Logic AND Gate [part_number=74HC08 package="DIP (Dual Inline) [THT]"]
  IC13 = IC, DIP package, 14 pins [chip_label=74HC04]
  S1 = Pushbutton [package="[THT]"]
  IC14 = IC, DIP package, 28 pins [chip_label="28C256-15 EEPROM"]
  IC15 = IC, DIP package, 14 pins [chip_label=74HC04]
  IC16 = IC, DIP package, 28 pins [chip_label="CY7C199-35PC SRAM"]
  IC17 = IC, DIP package, 14 pins [chip_label=74LS32]  # not connected
  IC18 = IC, DIP package, 14 pins [chip_label=74LS32]  # not connected
  IC19 = IC, DIP package, 14 pins [chip_label=74LS32]  # not connected
  IC20 = IC, DIP package, 14 pins [chip_label=74LS32]
  U8 = SWITCH_SPDT [package=kps-1290]
  U9 = 74HC595 [package="DIP16 [THT]"]  # not connected
  U10 = 74HC595 [package="DIP16 [THT]"]  # not connected
  U11 = 74HC595 [package="DIP16 [THT]"]  # not connected
  U12 = SWITCH_SPDT [package=kps-1290]  # not connected
  U13 = SWITCH_SPDT [package=kps-1290]  # not connected
  U14 = SWITCH_SPDT [package=kps-1290]  # not connected
  U15 = SWITCH_SPDT [package=kps-1290]  # not connected
  U16 = SWITCH_SPDT [package=kps-1290]  # not connected
  U17 = SWITCH_SPDT [package=kps-1290]  # not connected
  U18 = SWITCH_SPDT [package=kps-1290]  # not connected
  U19 = SWITCH_SPDT [package=kps-1290]  # not connected
  U20 = SWITCH_SPDT [package=kps-1290]  # not connected
  U21 = SWITCH_SPDT [package=kps-1290]  # not connected
  IC21 = IC, DIP package, 14 pins [chip_label=74HC04]
  U22 = POT [package=3362u]  # not connected
  LCD1 = LCD screen  # not connected
  U23 = mini DIN 6 Connector [package=mini-din6]
  C2 = Ceramic Capacitor [capacitance=0.1µF package="200 mil [THT, multilayer]"]
  C3 = Ceramic Capacitor [capacitance=0.1µF package="200 mil [THT, multilayer]"]
  C4 = Ceramic Capacitor [capacitance=0.1µF package="200 mil [THT, multilayer]"]
  C5 = Ceramic Capacitor [capacitance=0.1µF package="200 mil [THT, multilayer]"]
  C6 = Ceramic Capacitor [capacitance=0.1µF package="200 mil [THT, multilayer]"]
  C7 = Electrolytic Capacitor [capacitance=220µF package="100 mil [THT, electrolytic]"]
  C8 = Electrolytic Capacitor [capacitance=220µF package="100 mil [THT, electrolytic]"]
  R1 = Resistor [tolerance=±5% resistance=10k package="2512 [SMD]"]
  R2 = Resistor [tolerance=±5% resistance=5k package="2512 [SMD]"]
  R3 = Resistor [tolerance=±5% resistance=10k package="2512 [SMD]"]
  R4 = Resistor [tolerance=±5% resistance=3.3k package="2512 [SMD]"]
  R5 = Resistor [tolerance=±5% resistance=5k package="2512 [SMD]"]
  C9 = Electrolytic Capacitor [capacitance=220µF package="100 mil [THT, electrolytic]"]
  C10 = Electrolytic Capacitor [capacitance=220µF package="100 mil [THT, electrolytic]"]
  C11 = Electrolytic Capacitor [capacitance=47µF package="100 mil [THT, electrolytic]"]
  C12 = Ceramic Capacitor [capacitance=0.1µF package="200 mil [THT, multilayer]"]
  C13 = Ceramic Capacitor [capacitance=0.1µF package="200 mil [THT, multilayer]"]
  C14 = Electrolytic Capacitor [capacitance=22µF package="100 mil [THT, electrolytic]"]
  C15 = Electrolytic Capacitor [capacitance=22µF package="100 mil [THT, electrolytic]"]
  C16 = Ceramic Capacitor [capacitance=0.01µF package="200 mil [THT, multilayer]"]
  R6 = Resistor [tolerance=±5% resistance=3.3k package="2512 [SMD]"]
  R7 = Resistor [tolerance=±5% resistance=3.3k package="2512 [SMD]"]
  R8 = Resistor [tolerance=±5% resistance=3.3k package="2512 [SMD]"]
  C17 = Ceramic Capacitor [capacitance=0.1µF package="200 mil [THT, multilayer]"]
  C18 = Ceramic Capacitor [capacitance=0.1µF package="200 mil [THT, multilayer]"]
  R9 = Resistor [tolerance=±5% resistance=3.3k package="2512 [SMD]"]
  C19 = Electrolytic Capacitor [capacitance=220µF package="100 mil [THT, electrolytic]"]
  C20 = Electrolytic Capacitor [capacitance=220µF package="100 mil [THT, electrolytic]"]

nets:
  N1: IC1.1A, IC9.pin2
  N2: IC1.1B, IC9.pin4
  N3: IC1.1Y, U3.ST_CP, U4.ST_CP, IC9.pin5, IC10.pin5
  N4: IC1.2A, IC2.pin17, IC8.pin25, IC13.pin13
  N5: IC1.2B, IC9.pin6
  N6: IC1.2Y, IC21.pin1
  GND: IC1.GND, IC2.pin1, IC2.pin10, IC3.pin1, IC3.pin5, IC3.pin7, IC3.pin10, IC4.pin1, IC4.pin9, IC4.pin10, IC5.GND, Q1.C, IC6.pin8, Q2.C, U3.Q6, U3.GND, U3.OE, U4.GND, U4.OE, IC7.pin10, IC7.pin16, IC8.pin21, IC8.pin31, IC9.pin7, IC10.pin7, IC11.IN, XTAL1.pin_1, IC12.GND, IC13.pin7, S1.Pin_3, S1.Pin_4, IC15.pin7, IC16.pin14, U23.2, C2.0, C3.1, C5.1, C6.1, C7.-, C8.-, C9.-, C10.-, C11.-, C12.0, C13.0, C14.+, C15.-, C16.1, C17.1, C18.0, C19.-, C20.-
  N7: IC1.4Y, IC9.pin9
  N8: IC1.4A, IC9.pin10
  N9: IC1.4B, IC9.pin12
  VCC: IC1.VCC, IC2.pin3, IC2.pin5, IC2.pin7, IC2.pin9, IC2.pin12, IC2.pin14, IC2.pin16, IC2.pin18, IC2.pin20, IC3.pin3, IC3.pin9, IC3.pin12, IC3.pin14, IC3.pin16, IC3.pin18, IC3.pin20, IC4.pin3, IC4.pin5, IC4.pin7, IC4.pin12, IC4.pin14, IC4.pin16, IC4.pin18, IC4.pin20, IC5.VCC, IC6.pin7, IC6.pin9, IC6.pin10, IC6.pin16, U3.MR, U3.VCC, U4.MR, U4.VCC, IC7.pin20, U5.O, IC8.pin8, IC8.pin18, IC8.pin38, IC9.pin14, IC10.pin14, IC11.OUT, XTAL1.pin_0, IC12.VCC, IC13.pin14, IC14.pin28, IC15.pin14, IC16.pin24, IC16.pin28, U23.1, C2.1, C4.0, C5.0, C7.+, C8.+, R2.Pin_0, R4.Pin_0, R5.Pin_0, C9.+, C10.+, C11.+, C12.1, C13.1, C15.+, C16.0, R6.Pin_0, R7.Pin_1, R8.Pin_1, C17.0, C18.1, R9.Pin_0, C19.+, C20.+
  N10: IC2.pin2, IC8.pin17, IC16.pin25
  N11: IC2.pin6, IC8.pin19, IC16.pin21
  N12: IC2.pin8, IC8.pin20, IC16.pin23
  N13: IC2.pin11, IC8.pin22, IC16.pin2
  N14: IC2.pin13, IC8.pin23, IC16.pin26
  N15: IC2.pin15, IC8.pin24, IC16.pin1
  N16: IC2.pin19, IC9.pin1, IC9.pin13
  N17: IC3.pin2, IC4.pin2, IC8.pin9, IC16.pin10
  N18: IC3.pin4, IC4.pin4, IC8.pin10, IC16.pin9
  N19: IC3.pin6, IC4.pin6, IC8.pin11, IC16.pin8
  N20: IC3.pin8, IC4.pin8, IC8.pin12, IC16.pin7
  N21: IC3.pin11, IC4.pin11, IC8.pin13, IC16.pin6
  N22: IC3.pin13, IC4.pin13, IC8.pin14, IC16.pin5
  N23: IC3.pin15, IC4.pin15, IC8.pin15, IC16.pin4
  N24: IC3.pin17, IC4.pin17, IC8.pin16, IC16.pin3
  N25: IC3.pin19, IC9.pin11
  N26: IC4.pin19, IC9.pin3
  N27: IC5.3Y, R1.Pin_0, R3.Pin_1
  N28: IC5.3A, IC6.pin11
  N29: IC5.3B, IC5.4Y
  N30: IC5.4A, IC6.pin13
  N31: IC5.4B, IC6.pin14
  N32: Q1.E, IC10.pin3, U23.6, R2.Pin_1
  N33: Q1.B, R1.Pin_1
  N34: IC6.pin1, IC9.pin8
  N35: IC6.pin2, U3.SH_CP, U4.SH_CP, IC10.pin4
  N36: Q2.E, IC8.pin4, R4.Pin_1
  N37: Q2.B, R3.Pin_0
  N38: U3.Q2, IC7.pin11
  N39: U3.Q3, IC7.pin8
  N40: U3.Q4, IC7.pin13
  N41: U3.Q5, IC7.pin6
  N42: U3.Q7, IC7.pin4
  N43: U3.Q7', U4.DS
  N44: U3.DS, U23.5, R5.Pin_1
  N45: U4.Q1, IC7.pin2
  N46: U4.Q0, IC7.pin17
  N47: IC7.pin1, IC7.pin19, U5.P
  N48: IC7.pin3, IC8.pin32, IC16.pin13
  N49: IC7.pin5, IC8.pin30, IC16.pin15
  N50: IC7.pin7, IC8.pin28, IC16.pin17
  N51: IC7.pin9, IC8.pin26, IC16.pin19
  N52: IC7.pin12, IC8.pin27, IC16.pin18
  N53: IC7.pin14, IC8.pin29, IC16.pin16
  N54: IC7.pin18, IC8.pin33, IC16.pin12
  N55: U5.S, IC10.pin6
  N56: IC8.pin2, R7.Pin_0
  N57: IC8.pin6, R8.Pin_0
  N58: IC8.pin34, IC15.pin1, IC15.pin11
  N59: IC8.pin36, U6.P
  N60: IC8.pin39, IC12.3B
  N61: IC8.pin40, S1.Pin_1, S1.Pin_2, R9.Pin_1
  N62: U6.S, R6.Pin_1
  N63: IC11.GND, C14.-
  N64: IC12.3Y, IC15.pin3
  N65: IC12.3A, IC15.pin2
  N66: IC12.4Y, IC13.pin11
  N67: IC12.4A, IC13.pin12
  N68: IC12.4B, IC20.pin11
  N69: IC13.pin10, U8.S
  N70: IC15.pin4, IC16.pin27
  N71: IC15.pin10, IC16.pin22
  N72: IC16.pin20, U8.P

notes:
  PS/2 Keyboard
  Data
  Clock
  To 9V DC
  To GND
